# Fritzing sketch Stripboard (saved by Fritzing 0.9.6b)
stripboards: 2

parts:
  J1 = Thonkiconn PJ398SM [part_number=PJ398SM]
  J2 = Thonkiconn PJ398SM [part_number=PJ398SM]
  J3 = Thonkiconn PJ398SM [part_number=PJ398SM]
  J4 = Thonkiconn PJ398SM [part_number=PJ398SM]
  J5 = Thonkiconn PJ398SM [part_number=PJ398SM]
  U1 = POT [package=alps_pot]
  S3 = Taiway 100-SP-X-T1 SPDT Miniature Toggle Switch [part_number=100-SP-X-T1-0-0-B1-M2 package=THT]
  S6 = adafruit
  S7 = adafruit
  JP1 = Header 4 [package=jst-4-pth]
  JP2 = Header 3 [package=molex-1x3_lock]
  JP3 = Header 4 [package=jst-4-pth]
  LED1 = LED Red 3mm - Top View [package="3 mm [THT] Top View"]
  LED2 = LED Red 3mm - Top View [package="3 mm [THT] Top View"]
  R3 = Vertical Resistor [tolerance=±5% resistance=220 package=THT]
  R4 = Vertical Resistor [tolerance=±5% resistance=220 package=THT]
  R5 = Vertical Resistor [tolerance=±5% resistance=220 package=THT]
  LED3 = LED Red 3mm - Top View [package="3 mm [THT] Top View"]
  LED4 = LED Red 3mm - Top View [package="3 mm [THT] Top View"]
  R6 = Vertical Resistor [tolerance=±5% resistance=220 package=THT]
  ENCODER1 = Rotary Encoder with Knob
  JP4 = Header 4 [package=jst-4-pth]
  JP5 = Header 3 [package=molex-1x3_lock]
  JP6 = Header 2 [package=molex-1x2_lock]

nets:
  N1: J1.Pin_1, J2.Pin_1, J3.Pin_1, J4.Pin_1, J5.Pin_1, U1.A, S6.connector0, S6.connector3, S7.connector0, S7.connector3, JP1.1, LED1.cathode, LED2.cathode, LED3.cathode, LED4.cathode
  N2: J1.Pin_2, J2.Pin_2, J3.Pin_2, J4.Pin_2
  N3: J1.Pin_3, JP3.4, R3.Pin_1
  N4: J2.Pin_3, JP3.3, R4.Pin_1
  N5: J3.Pin_3, JP3.2, R5.Pin_1
  N6: J4.Pin_3, JP3.1, R6.Pin_1
  N7: J5.Pin_3, JP2.3
  N8: U1.E, JP1.2
  N9: U1.S, JP2.1
  N10: S3.L1, JP2.2
  N11: S6.connector2, S6.connector4, JP1.3
  N12: S7.connector2, S7.connector4, JP1.4
  N13: LED1.anode, R3.Pin_0
  N14: LED2.anode, R4.Pin_0
  N15: R5.Pin_0, LED3.anode
  N16: LED4.anode, R6.Pin_0
  N17: ENCODER1.no_name_yet#1, JP4.4
  N18: ENCODER1.no_name_yet#2, ENCODER1.no_name_yet#4, JP4.3, JP5.3
  N19: ENCODER1.no_name_yet#3, JP4.2
  N20: ENCODER1.no_name_yet#5, JP4.1
  N21: JP5.1, JP6.2
  N22: JP5.2, JP6.1

notes:
  Right Button
  Left Button
  Vcc
  GND
  Ext Clock
  Ext/Int Toggle
  Rate Pot
  Gate 1
  Gate 2
  Gate 3
  Gate 4
  NeoPixels Connector
  GND
  Vcc
  Data
  Enc Button
  Enc A
  GND
  ENC B
  Vcc
  NeoPixels Data

custom parts:
  Thonkiconn PJ398SM: PJ398SM
  LED Red 3mm - Top View: A generic red LED (~1.8V)
  Vertical Resistor: A generic resistor (0.25W)
  Rotary Encoder with Knob: Rotary Encoder with 1/4" Shaft and Knob
