# Fritzing sketch nano-euclid (saved by Fritzing 0.9.6b)
breadboards: 1

parts:
  Part1 = Arduino Nano Every
  PLAY/STOP = Round Pushbutton
  CHAN = Round Pushbutton
  ENCODER1 = Rotary Encoder with Knob
  INT/EXT = Toggle Switch [package=THT]
  Q1 = NPN-Transistor [package="TO92 [THT]"]
  TEMPO = Rotary Potentiometer (Small) [maximum_resistance=100kΩ package=THT]
  J1 = Screw terminal - 2 pins [package=THT]
  J2 = Screw terminal - 2 pins [package=THT]
  J3 = Screw terminal - 2 pins [package=THT]
  J4 = Screw terminal - 2 pins [package=THT]
  J5-CLK_IN = Screw terminal - 2 pins [package=THT]
  R4 = Resistor [tolerance=±5% power=0.25 resistance=10k package=THT]
  R5 = Resistor [tolerance=±5% power=0.25 resistance=10k package=THT]
  POWER = Screw terminal - 2 pins [package=THT]
  Part2 = 16 NeoPixel Ring [part_number=1463]
  R6 = Resistor [tolerance=±5% power=0.25 resistance=1M package=THT]
  ON/OFF = Toggle Switch [package=THT]

nets:
  N1: Part1.RESET, Part1.A7
  GND: Part1.GND, Part1.D13~, ENCODER1.no_name_yet#2, INT/EXT.COM, Q1.E, TEMPO.leg1, J1.pin1, J2.pin1, J3.pin1, J4.pin1, J5-CLK_IN.pin1, R4.Pin_1, POWER.pin1, Part2.GND
  N2: Part1.D2, J4.pin2
  N3: Part1.D3~, J3.pin2
  N4: Part1.D4, J2.pin2
  N5: Part1.D5~, J1.pin2
  N6: Part1.D6~, Part2.IN
  N7: Part1.D7, ENCODER1.no_name_yet#3
  N8: Part1.D8, ENCODER1.no_name_yet#1
  N9: Part1.D9~, ENCODER1.no_name_yet#4
  N10: Part1.D10~, Q1.C, R5.Pin_1
  N11: Part1.D11/MOSI, Part1.+5V, PLAY/STOP.leg1
  N12: Part1.D12~/MISO, INT/EXT.L2
  VIN: Part1.VIN, TEMPO.leg2, R5.Pin_0, Part2.VDD, ON/OFF.L2
  N13: Part1.A3, CHAN.leg1, R6.Pin_0
  N14: Part1.A1, TEMPO.wiper
  N15: PLAY/STOP.leg0, CHAN.leg0
  N16: J5-CLK_IN.pin2, R4.Pin_0
  N17: POWER.pin2, ON/OFF.COM

custom parts:
  Arduino Nano Every: The Nano Every is Arduino’s 5V compatible board in the smallest available form factor: 45x18mm! The Arduino Nano is the preferred board for many projects requiring a small and easy to use microcontroller board. The small footprint and low price, make the Nano Every particularly suited for wearable inventions, low cost robotics, electronic musical instruments, and general use to control smaller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
  Rotary Encoder with Knob: Rotary Encoder with 1/4" Shaft and Knob
  16 NeoPixel Ring: 16 ultra bright smart LED NeoPixels are arranged in a circle with 1.75" (44.5mm) outer diameter. The rings are 'chainable' - connect the output pin of one to the input pin of another. Use only one microcontroller pin to control as many as you can chain together! Each LED is addressable as the driver chip is inside the LED. Each one has ~18mA constant current drive so the color will be very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
